# Fritzing sketch treenhouse sketch (saved by Fritzing 0.9.3b)
perfboards: 1

parts:
  Bauteil1 = Arduino Uno (Rev3) - ICSP
  Bauteil2 = Barometric Pressure Sensor - BMP085 Breakout
  DS1 = DS18B20 1-Wire Temperature Sensor [part_number=DS18B20]  # not connected
  ZS-042_RTC1 = ZS-042 RTC Module
  U1 = Voltage Regulator [package=to220-adj]
  Power_plug1 = Power plug
  C1 = Electrolytic Capacitor [capacitance=1µF package="100 mil [THT, electrolytic]"]
  R2 = Resistor [tolerance=±5% resistance=220 package=THT]
  R3 = Resistor [tolerance=±5% resistance=220 package=THT]
  C2 = Tantalum Capacitor [capacitance=0.1µF package="100 mil [THT, tantalum]"]
  U2 = ESP8266 WiFi Module [part_number=ESP8266]
  HC-SR04_Sensor_1 = HC-SR04 Ultrasonic Distance Sensor  # not connected
  J1 = double row female pin header, 4 pins [form="♀ (female)"]
  J2 = double row female pin header, 6 pins [form="♀ (female)"]
  RHT1 = Humidity and Temperature Sensor RHT03  # not connected
  R4 = Resistor [tolerance=±5% resistance=220 package=THT]

nets (from the breadboard view):
  N1: Bauteil1.A2, J1.pin3
  N2: Bauteil1.A3, J2.pin4, R4.Pin_1
  N3: Bauteil1.A4/SDA, J1.pin2
  N4: Bauteil1.A5/SCL, ZS-042_RTC1.SCL
  N5: Bauteil1.D0/RX, U2.RXD
  N6: Bauteil1.D1/TX, U2.TXD
  N7: Bauteil1.D7, J2.pin3
  VCC: Bauteil2.VCC, U1.OUT, C1.+, R2.Pin_0, U2.VCC
  GND: Bauteil2.GND, ZS-042_RTC1.GND, Power_plug1.GND, C1.-, R3.Pin_1, C2.-, U2.GND, J1.pin4, J2.pin5
  VCC_2: ZS-042_RTC1.VCC, U1.IN, Power_plug1.VCC, C2.+, J1.pin1, J2.pin6, R4.Pin_0
  N8: U1.ADJ, R2.Pin_1, R3.Pin_0

custom parts:
  ESP8266 WiFi Module: Generic WiFi Module based on the ESP8266 with onboard PCB antenna and UART communications
